# Fritzing sketch Teensy Gogogo Connection (saved by Fritzing 0.9.4)
breadboards: 1

parts:
  Go_go_go1 = Go go go Motor Driver  # not connected
  Teensy1 = Teensy 3.1  # not connected
  LED1 = smd LED [color="Green (555nm)" package="0805 [SMD]"]
  LED2 = smd LED [color="Red (633nm)" package="0805 [SMD]"]
  LED3 = smd LED [color="Green (555nm)" package="0805 [SMD]"]
  LED4 = smd LED [color="Red (633nm)" package="0805 [SMD]"]
  LED5 = smd LED [color="Green (555nm)" package="0805 [SMD]"]
  LED6 = smd LED [color="Red (633nm)" package="0805 [SMD]"]
  LED8 = smd LED [color="Red (633nm)" package="0805 [SMD]"]
  LED10 = smd LED [color="Red (633nm)" package="0805 [SMD]"]
  LED11 = smd LED [color="Green (555nm)" package="0805 [SMD]"]
  LED12 = smd LED [color="Green (555nm)" package="0805 [SMD]"]

nets:
  N1: LED1.cathode, LED2.anode, LED3.cathode, LED4.anode, LED5.cathode, LED6.anode, LED8.anode, LED10.anode, LED11.cathode, LED12.cathode
  N2: LED1.anode, LED2.cathode, LED3.anode, LED4.cathode, LED5.anode, LED8.cathode, LED10.cathode, LED11.anode, LED12.anode

custom parts:
  Teensy 3.1: The Teensy is a complete USB-based microcontoller development system, in a very small footprint, capable of implementing many types of projects. All programming is done via the USB port. No special programmer is needed, only a standard micro-USB cable and a PC or Macintosh with a USB port. It has a USB keyboard/mouse/joystick emulation stack and can be programmed through Arduino IDE.
